# Fritzing sketch Team-SR-Robo (saved by Fritzing 0.9.3b)
breadboards: 1

parts:
  pyboard1 = Micro Python pyboard [part_number=PYBv10b]
  LED1 = smd LED [color="Red (633nm)" package="0603 [SMD]"]
  R1 = Resistor [tolerance=±5% resistance=360 package=THT]
  R3 = Resistor [tolerance=±5% resistance=360 package=THT]
  LED2 = smd LED [color="Red (633nm)" package="0603 [SMD]"]
  hc-sr1 = hc-sr04

nets:
  N1: pyboard1.P9A_GND, LED1.cathode, LED2.cathode, hc-sr1.GND
  N2: pyboard1.X1, R1.Pin_1
  N3: pyboard1.X2, R3.Pin_1
  N4: pyboard1.X5, hc-sr1.Echo
  N5: pyboard1.X6, hc-sr1.Trig
  N6: pyboard1.Y15_3V3, hc-sr1.VCC
  N7: LED1.anode, R1.Pin_0
  N8: R3.Pin_0, LED2.anode

// code stored in the sketch: Untitled.bas
import pyb

led1 = pyb.Pin('X1',pyb.Pin.OUT_PP)
led2 = pyb.Pin('X2',pyb.Pin.OUT_PP)
sw = pyb.switch()
y = int(input())
r = 2.54 /100
R = 2 * r 
rpm = 4000 
d=1
d1=1
d2=1
d3=3
d4=3
while True:
	if y==1:
		led1.on()
		led2.on()
		delay(((d1/(2*rpm*r)))*60*1000)
		led2.off()
		delay(((((R*3.14)/2)/(2*rpm*r)))*60*1000)
		led1.on()
		led2.on()
		delay(((d/(2*rpm*r)))*60*1000)
		led1.off()
		led2.off()
		while True:
			if sw.value():
				break
		led1.on()
		led2.off()
		delay(((2*((R*3.14)/2)/(2*rpm*r)))*60*1000)
		led1.on()
		led2.on()
		delay(((d/(2*rpm*r)))*60*1000)
		led1.off()
		led2.on()
		delay(((((R*3.14)/2)/(2*rpm*r)))*60*1000)
		led1.on()
		led2.on()
		delay(((d1/(2*rpm*r)))*60*1000)
		led1.off()
		led2.off()
		break
	elif y==2:
		led2.on()
		led1.on()
		delay(((d2/(2*rpm*r)))*60*1000)
		led1.off()
		delay(((((R*3.14)/2)/(2*rpm*r)))*60*1000)
		led2.on()
		led1.on()
		delay(((d/(2*rpm*r)))*60*1000)
		led2.off()
		led1.off()
		while True:
			if sw.value():
				break
		led2.on()
		led1.off()
		delay(((2*((R*3.14)/2)/(2*rpm*r)))*60*1000)
		led2.on()
		led1.on()
		delay(((d/(2*rpm*r)))*60*1000)
		led2.off()
		led1.on()
		delay(((((R*3.14)/2)/(2*rpm*r)))*60*1000)
		led2.on()
		led1.on()
		delay(((d2/(2*rpm*r)))*60*1000)
		led2.off()
		led1.off()
		break
	elif y==3:
		led2.on()
		led1.on()
		delay(((d3/(2*rpm*r)))*60*1000)
		led1.off()
		delay(((((R*3.14)/2)/(2*rpm*r)))*60*1000)
		led2.on()
		led1.on()
		delay(((d/(2*rpm*r)))*60*1000)
		led2.off()
		led1.off()
		while True:
			if sw.value():
				break
		led2.on()
		led1.off()
		delay(((2*((R*3.14)/2)/(2*rpm*r)))*60*1000)
		led2.on()
		led1.on()
		delay(((d/(2*rpm*r)))*60*1000)
		led2.off()
		led1.on()
		delay(((((R*3.14)/2)/(2*rpm*r)))*60*1000)
		led2.on()
		led1.on()
		delay(((d3/(2*rpm*r)))*60*1000)
		led2.off()
		led1.off()
		break
	elif y==4:
		led1.on()
		led2.on()
		delay(((d4/(2*rpm*r)))*60*1000)
		led2.off()
		delay(((((R*3.14)/2)/(2*rpm*r)))*60*1000)
		led1.on()
		led2.on()
		delay(((d/(2*rpm*r)))*60*1000)
		led1.off()
		led2.off()
		while True:
			if sw.value():
				break
		led1.on()
		led2.off()
		delay(((2*((R*3.14)/2)/(2*rpm*r)))*60*1000)
		led1.on()
		led2.on()
		delay(((d/(2*rpm*r)))*60*1000)
		led1.off()
		led2.on()
		delay(((((R*3.14)/2)/(2*rpm*r)))*60*1000)
		led1.on()
		led2.on()
		delay(((d4/(2*rpm*r)))*60*1000)
		led1.off()
		led2.off()
		break
